# Fritzing sketch sketch (saved by Fritzing 0.9.6b)
breadboards: 1

parts:
  Part1 = Arduino Uno (Rev3)
  R1 = Resistor [tolerance=±5% power=0.25 resistance=220 package=THT]
  LED1 = LED - 5mm [color="Green (570nm)" current=0.030 package="5 mm [THT]"]
  LED2 = LED - 5mm [color="Red (660nm)" current=0.030 package="5 mm [THT]"]
  R2 = Resistor [tolerance=±5% power=0.25 resistance=220 package=THT]

nets:
  N1: Part1.D8, LED2.anode
  N2: Part1.D7, LED1.anode
  N3: Part1.GND, R1.Pin_0, R2.Pin_0
  N4: R1.Pin_1, LED1.cathode
  N5: LED2.cathode, R2.Pin_1
